# Fritzing sketch HR_Contact (saved by Fritzing 0.9.3b)
breadboards: 1

parts:
  MCU = Arduino Mega 2560 (Rev3)
  GND = female pin header, 1 pin [form="♀ (female)"]
  VDD_(+5V) = female pin header, 1 pin [form="♀ (female)"]
  P0_(pulse) = female pin header, 1 pin [form="♀ (female)"]
  R3 = Resistor [tolerance=±5% resistance=1k package=THT]
  R4 = Resistor [tolerance=±5% resistance=220 package=THT]
  LED1 = LED - 5mm [color="Red (633nm)" package="5 mm [THT]"]

nets:
  GND: MCU.GND, GND.pin1, LED1.cathode
  N1: MCU.5V, VDD_(+5V).pin1
  N2: MCU.D2_PWM, R3.Pin_0
  N3: MCU.D22, MCU.D23
  N4: MCU.D24, R4.Pin_0
  N5: P0_(pulse).pin1, R3.Pin_1
  N6: R4.Pin_1, LED1.anode

notes:
  polar hr receiver pins
  (J1 & J2 are the transmitters from the chest strap)
