# Fritzing sketch LightRelays (saved by Fritzing 0.9.3b)
breadboards: 1

parts:
  MCU = Arduino Mega 2560 (Rev3)
  8_Channel_Relay = 8 Channel Power Relay
  VCC1 = DC Power [voltage=12V]
  VCC2 = DC Power [voltage=5V]
  LED_Panel_1 = female pin header, 2 pins [form="♀ (female)"]
  LED_Panel_2 = female pin header, 2 pins [form="♀ (female)"]
  LED_Panel_3 = female pin header, 2 pins [form="♀ (female)"]
  LED_Panel_4 = female pin header, 2 pins [form="♀ (female)"]
  LED_Panel_5 = female pin header, 2 pins [form="♀ (female)"]
  LED_Panel_6 = female pin header, 2 pins [form="♀ (female)"]
  LED_Panel_7 = female pin header, 2 pins [form="♀ (female)"]
  LED_Panel_8 = female pin header, 2 pins [form="♀ (female)"]
  C1 = Ceramic Capacitor [capacitance=100nF package="100 mil [THT, multilayer]"]
  C2 = Ceramic Capacitor [capacitance=100nF package="100 mil [THT, multilayer]"]

nets:
  5V: MCU.5V, 8_Channel_Relay.VCC
  N1: MCU.D25, 8_Channel_Relay.IN1
  N2: MCU.D26, 8_Channel_Relay.IN2
  N3: MCU.D27, 8_Channel_Relay.IN3
  N4: MCU.D28, 8_Channel_Relay.IN4
  N5: MCU.D29, 8_Channel_Relay.IN5
  N6: MCU.D30, 8_Channel_Relay.IN6
  N7: MCU.D31, 8_Channel_Relay.IN7
  N8: MCU.D32, 8_Channel_Relay.IN8
  GND: 8_Channel_Relay.GND, VCC1.V-, VCC2.V-, LED_Panel_1.pin2, LED_Panel_2.pin2, LED_Panel_3.pin2, LED_Panel_4.pin2, LED_Panel_5.pin2, LED_Panel_6.pin2, LED_Panel_7.pin2, LED_Panel_8.pin2, C1.0, C2.0
  N9: 8_Channel_Relay.JD-VCC, VCC2.V+, C2.1
  N10: 8_Channel_Relay.COM, VCC1.V+, C1.1
  N11: 8_Channel_Relay.NO#23, LED_Panel_1.pin1
  N12: 8_Channel_Relay.NO#26, LED_Panel_2.pin1
  N13: 8_Channel_Relay.NO#29, LED_Panel_3.pin1
  N14: 8_Channel_Relay.NO#32, LED_Panel_4.pin1
  N15: 8_Channel_Relay.NO#35, LED_Panel_5.pin1
  N16: 8_Channel_Relay.NO#38, LED_Panel_6.pin1
  N17: 8_Channel_Relay.NO#41, LED_Panel_7.pin1
  N18: 8_Channel_Relay.NO#44, LED_Panel_8.pin1

notes:
  8-channel relay board for driving the LED panels. Note that the Arduino is NOT conncted to the ground of this circuit. That is because the relay board has an optooscillator (basically an LED and phototransistor) that is used to electrically isolate the relays from the rest of your circuit. This is for safety. The Arduino will be tied to a separate ground

custom parts:
  8 Channel Power Relay: An 8 channel power relay. The module operates at 5V.
