# Fritzing sketch Peltier (saved by Fritzing 0.9.3b)
breadboards: 1

parts:
  TEC = Peltier Element
  Q1 = MOSFET-NCHANNEL [part_number=IRLB8721 package=to220v]
  VCC = DC Power [voltage=12V]
  R1 = Resistor [tolerance=±5% resistance=220 package=THT]
  R2 = Resistor [tolerance=±5% resistance=10k package=THT]
  D1 = Rectifier Diode [part_number=1N4004 package="300 mil [THT]"]
  R3 = Temperature Sensor (Thermistor) [thermistor_type=NTC package=THT]
  R4 = Resistor [tolerance=±1% resistance=10k package=THT]
  Fan = Fan - Ventilador [package=THT]
  D2 = Rectifier Diode [part_number=1N4004 package="300 mil [THT]"]
  Q2 = MOSFET-NCHANNEL [part_number=IRLB8721 package=to220v]
  R5 = Resistor [tolerance=±5% resistance=220 package=THT]
  R6 = Resistor [tolerance=±5% resistance=10k package=THT]
  MCU = Arduino Mega 2560 (Rev3)
  C1 = Ceramic Capacitor [capacitance=100nF package="100 mil [THT, multilayer]"]

nets:
  N1: TEC.pin1, VCC.V+, D1.cathode, Fan.5V, D2.cathode
  N2: TEC.pin2, Q1.D, D1.anode
  N3: Q1.G, R1.Pin_1, R2.Pin_0
  GND: Q1.S, VCC.V-, R2.Pin_1, R3.pin_1, Q2.S, R6.Pin_1, MCU.GND, C1.0
  N4: R1.Pin_0, MCU.D4_PWM
  N5: R3.pin_0, R4.Pin_0, MCU.A0
  N6: R4.Pin_1, MCU.D38
  N7: Fan.GND, D2.anode, Q2.D
  N8: Q2.G, R5.Pin_1, R6.Pin_0
  N9: R5.Pin_0, MCU.D5_PWM

notes:
  circuit for driving the Peltier/thermoelectric cooler and fan assembly
  for two assemblies just double the components

custom parts:
  Fan - Ventilador: Ventilador de 2 pines, se encuentra comunmente en computadoras de escritorio
