# Fritzing sketch dotstar_darkfield_illumnator (saved by Fritzing 0.9.3b)
breadboards: 1

parts:
  DOTSTAR1 = DotStar Strip -- White (60/m) [part_number=2240]
  Part1 = Arduino Mega 2560 (Rev3)
  R1 = Resistor [tolerance=±5% resistance=470 package=THT]
  C2 = Capacitor Polarized [part_number=10000uF package=panasonic_h13]

nets:
  N1: DOTSTAR1.DI, R1.Pin_0
  GND: DOTSTAR1.GND, Part1.GND, C2.-
  5V: DOTSTAR1.+5V, C2.+
  N2: DOTSTAR1.CI, Part1.D52
  N3: Part1.D51, R1.Pin_1

custom parts:
  DotStar Strip -- White (60/m): NeopixelDotStar Strip, White, 60 pixels per meter.
